// Logisim project Projeto extreme.circ as structural Verilog
module \cronômetro  (
);

  wire and_1_out, and_2_out, button_1_out, clock_1_out, register_2_q, subtractor_2_out;
  wire [3:0] register_1_q, register_3_q, subtractor_1_out, subtractor_3_out;

  Subtractor #(.width(4)) subtractor_1 (.a(register_1_q), .b(4'b0001), .out(subtractor_1_out));  // open: bin, bout
  Register #(.width(4), .Select("low")) register_1 (
    .D(subtractor_1_out), .Q(register_1_q), .clk(and_1_out));  // open: en, clr
  and and_1 (and_1_out, clock_1_out, register_2_q);
  Clock clock_1 (.out(clock_1_out));
  Hex_Digit_Display hex_digit_display_1 (.value(register_1_q));  // open: dp
  Subtractor #(.width(1)) subtractor_2 (.a(1'b1), .b(register_2_q), .out(subtractor_2_out));  // open: bin, bout
  Register #(.width(1), .Select("low")) register_2 (
    .D(subtractor_2_out), .Q(register_2_q), .clk(button_1_out));  // open: en, clr
  Subtractor #(.width(4)) subtractor_3 (.a(register_3_q), .b(4'b0001), .out(subtractor_3_out));  // open: bin, bout
  and and_2 (and_2_out, ~register_2_q, clock_1_out);  // AND_Gate
  Button button_1 (.out(button_1_out));
  Hex_Digit_Display hex_digit_display_2 (.value(register_3_q));  // open: dp
  Register #(.width(4), .Select("low")) register_3 (
    .D(subtractor_3_out), .Q(register_3_q), .clk(and_2_out));  // open: en, clr
endmodule
